# Fritzing sketch jeenode_bmp085_dht22_433mhzfsk (saved by Fritzing 0.9.0b)
stripboards: 1

parts:
  Part1 = Barometric Pressure Sensor - BMP085 Breakout
  VY-MK-5V_(433mhz) = Humidity and Temperature Sensor RHT03
  DHT22 = Humidity and Temperature Sensor RHT03
  R1 = Resistor [tolerance=±5% resistance=10k package=THT]
  R2 = Resistor [tolerance=±5% resistance=3.3k package=THT]
  R3 = Resistor [tolerance=±5% resistance=1.8k package=THT]
  Part2 = JeeNode wireless microcontroller

nets (from the schematic view):
  GND: Part1.GND, VY-MK-5V_(433mhz).GND_2, DHT22.GND_1, R2.Pin_0, Part2.GND
  N1: Part1.SCL, Part2.A2
  3.3V: VY-MK-5V_(433mhz).Vcc, DHT22.Vcc, R1.Pin_0, Part2.VCC
  N2: DHT22.Data-signal, R1.Pin_1, Part2.DIO2
  N3: R2.Pin_1, R3.Pin_0, Part2.INT2

notes:
  P
  D
  G
  +(3v3)
  A
  I
  P3
  P2
  VCC
  GND
  SCL
  SDA
  DATA
